// Logisim project CPU-final.circ as structural Verilog: 15 circuits, main circuit main
module main (
  input  clr
);

  wire alu_1_equal, alu_1_gt, Branch, CLK, clock_1_out, comparator_1_eq, comparator_2_eq, comparator_3_eq,
       display, ex_mem_1_equal_2, ex_mem_1_gt_2, Halt, IF_ID_Rs_en, IF_ID_Rt_en, load_use, multiplexer_2_out,
       multiplexer_3_out, not_1_out, not_2_out, not_3_out, not_4_out, RegWrite;
  wire [1:0] Ex_Mem_Rd, Forword1, Forword2, id_ex_1_rd_2, id_ex_1_rs_2, id_ex_1_rt_2, mem_wr_1_regdst_2,
       multiplexer_5_out, PCSrc, Rd, Rs, Rt;
  wire [2:0] funct, id_ex_1_control_2;
  wire [3:0] ALUOp, id_ex_1_aluop_2, op;
  wire [6:0] mem_wr_1_control_2;
  wire [7:0] id_ex_1_imm_offset_2, imm;
  wire [11:0] id_ex_1_jaddr_2, jAddr;
  wire [12:0] id_ex_1_control_2_2;
  wire [12:1] ex_mem_1_control_2;
  wire [15:0] adder_2_out, alu_1_aluout, BranchAddr, CLKCounter, Control, controlled_buffer_1_out, d0, d1,
       dataredir_1_redirdata, dataredir_2_redirdata, EX_IR, ex_mem_1_aluout_2, ex_mem_1_rd2_2, id_ex_1_rd1_2,
       id_ex_1_rd2_2, ID_IR, IF_IR, Imm16, JumpAddr, jumpaddr_1_jumpaddr_2, MEM_IR, mem_wr_1_aluout_2,
       mem_wr_1_memout_2, multiplexer_1_out, multiplexer_4_out, multiplexer_6_out, multiplexer_7_out, PC1,
       PC2, PC3, PC4, PC5, PC_q, R_rs, R_rt, RAMValue, rg0, rg1, rg2, rg3, WR_IR;

  Multiplexer #(.select(2), .width(16), .enable("false")) multiplexer_1 (
    .in0(PC1), .in1(BranchAddr), .in2(JumpAddr), .out(multiplexer_1_out), .sel(PCSrc));  // open: in3
  not not_1 (not_1_out, load_use);
  Register #(.width(16)) PC (.D(multiplexer_1_out), .en(not_1_out), .Q(PC_q), .clk(CLK));  // open: clr
  and and_1 (CLK, clock_1_out, not_2_out);
  not not_2 (not_2_out, Halt);
  Clock clock_1 (.out(clock_1_out));
  Adder #(.width(16)) adder_1 (.a(16'h1), .b(PC_q), .out(PC1));  // open: cin, cout
  Counter #(.width(16), .max('hffff), .ongoal("continue")) counter_1 (
    .count(1'b1), .Q(CLKCounter), .clk(CLK), .clr(clr));  // open: load, D, carry
  Multiplexer #(.enable("false")) multiplexer_2 (
    .in0(display), .in1(1'b0), .out(multiplexer_2_out), .sel(comparator_1_eq));
  Comparator comparator_1 (.a(8'h1), .b(imm), .eq(comparator_1_eq));  // open: gt, lt
  Multiplexer #(.enable("false")) multiplexer_3 (
    .in0(display), .in1(1'b0), .out(multiplexer_3_out), .sel(comparator_2_eq));
  Comparator comparator_2 (.a({8{1'b0}}), .b(imm), .eq(comparator_2_eq));  // open: gt, lt
  Register #(.width(16)) register_1 (.D(R_rs), .en(multiplexer_2_out), .Q(d0), .clk(CLK), .clr(1'b0));
  Register #(.width(16)) register_2 (.D(R_rs), .en(multiplexer_3_out), .Q(d1), .clk(CLK), .clr(1'b0));
  ROM #(.addrWidth(16), .dataWidth(16)) rom_1 (.addr(PC_q), .data(IF_IR), .sel(1'b1));
  // Probe on IF_IR
  Hex_Digit_Display hex_digit_display_1 (.value(d0[11:8]));  // open: dp
  Hex_Digit_Display hex_digit_display_2 (.value(d0[15:12]));  // open: dp
  Hex_Digit_Display hex_digit_display_3 (.value(d1[11:8]));  // open: dp
  Hex_Digit_Display hex_digit_display_4 (.value(d1[15:12]));  // open: dp
  IF_ID if_id_1 (
    .Instruction(IF_IR), .Instruction_2(ID_IR), .PC_1(PC1), .PC_1_2(PC2), .Clock(CLK), .Clear(Branch),
    .enable(not_3_out));
  IR ir_1 (
    .opcode(op), .Rs(Rs), .Rt(Rt), .Rd(Rd), .funct(funct), .Input(ID_IR), .jAddr(jAddr), .offset(imm),
    .imm(imm));  // open: shamt
  not not_3 (not_3_out, load_use);
  Hex_Digit_Display hex_digit_display_5 (.value(d0[7:4]));  // open: dp
  Hex_Digit_Display hex_digit_display_6 (.value(d0[3:0]));  // open: dp
  Hex_Digit_Display hex_digit_display_7 (.value(d1[3:0]));  // open: dp
  Hex_Digit_Display hex_digit_display_8 (.value(d1[7:4]));  // open: dp
  Multiplexer #(.width(16), .enable("false")) multiplexer_4 (
    .in0(ID_IR), .in1({16{1'b0}}), .out(multiplexer_4_out), .sel(load_use));
  // Probe on PC1
  // Probe on PC2
  // Probe on ID_IR
  // Probe on IF_IR
  // Probe on rg0
  // Probe on rg1
  // Probe on R_rs
  // Probe on R_rt
  Control control_1 (
    .display_11(display), .Control(Control), .aluFunc(ALUOp), .rtEnable_14(IF_ID_Rt_en),
    .rsEnable_13(IF_ID_Rs_en), .IR(multiplexer_4_out));  // open: beq_4, aluSource_2, memToReg_9, bne_5, memRead_8, bgt_6, Jump_3, regWrite_10, signExtend__0, RegDst_1, halt_12, memWrite_7
  // Probe on PC3
  // Probe on EX_IR
  // Probe on rg3
  // Probe on rg2
  // Probe on RAMValue
  RF rf_1 (
    .Read_register_1(Rs), .Read_register_2(Rt), .write_register(mem_wr_1_regdst_2),
    .write_data(multiplexer_7_out), .Read_Data_1(R_rs), .Read_Data_2(R_rt), .Reg_0_Value(rg0),
    .Reg_1_Value(rg1), .Reg_2_Value(rg2), .Reg_3_Value(rg3), .RegWrite(RegWrite), .clock(CLK));
  // Probe on PC4
  // Probe on MEM_IR
  // Probe on CLKCounter
  ID_EX id_ex_1 (
    .Control(Control), .clock(CLK), .RD1(R_rs), .RD2(R_rt), .Rd(Rd), .RD1_2(id_ex_1_rd1_2),
    .RD2_2(id_ex_1_rd2_2), .Rd_2(id_ex_1_rd_2), .Pc_4_2(PC3), .pc_4(PC2),
    .Control_2({id_ex_1_control_2_2, id_ex_1_control_2}), .imm_offset(imm),
    .imm_offset_2(id_ex_1_imm_offset_2), .jAddr(jAddr), .jAddr_2(id_ex_1_jaddr_2), .Rt(Rt),
    .Rt_2(id_ex_1_rt_2), .ALUOp_2(id_ex_1_aluop_2), .Rs(Rs), .Rs_2(id_ex_1_rs_2), .ALUOp(ALUOp),
    .clear(Branch), .IR(ID_IR), .IR_2(EX_IR));
  Load_useControl load_usecontrol_1 (
    .ID_EX_MemRead(id_ex_1_control_2_2[5]), .ID_EX_Rt(id_ex_1_rt_2), .IF_ID_Rs(Rs), .IF_ID_Rt(Rt),
    .ID_EX_Rs_en(IF_ID_Rs_en), .ID_EX_Rt_en(IF_ID_Rt_en), .load_use(load_use), .IR(EX_IR));
  // Probe on PC5
  // Probe on WR_IR
  SignExtend signextend_1 (
    .imm_offset(id_ex_1_imm_offset_2), .extendOp(id_ex_1_control_2[0]), .extended_imm_offset(Imm16));
  Multiplexer #(.width(2), .enable("false")) multiplexer_5 (
    .in0(id_ex_1_rt_2), .in1(id_ex_1_rd_2), .out(multiplexer_5_out), .sel(id_ex_1_control_2[1]));
  JumpAddr jumpaddr_1 (.PC(PC3), .JumpAddr(id_ex_1_jaddr_2), .jumpAddr_2(jumpaddr_1_jumpaddr_2));
  Adder #(.width(16)) adder_2 (.a(PC3), .b(Imm16), .out(adder_2_out));  // open: cin, cout
  DataRedir dataredir_1 (
    .Forward(Forword1), .rawData(id_ex_1_rd1_2), .memData(multiplexer_7_out), .wbData(ex_mem_1_aluout_2),
    .redirData(dataredir_1_redirdata));
  DataRedir dataredir_2 (
    .Forward(Forword2), .rawData(id_ex_1_rd2_2), .memData(multiplexer_7_out), .wbData(ex_mem_1_aluout_2),
    .redirData(dataredir_2_redirdata));
  DataHazardsControl datahazardscontrol_1 (
    .EX_MEM_Rd(Ex_Mem_Rd), .MEM_WB_Rd(mem_wr_1_regdst_2), .ID_EX_Rs(id_ex_1_rs_2), .ID_EX_Rt(id_ex_1_rt_2),
    .EX_RegWrite(ex_mem_1_control_2[7]), .Mem_RegWrite(RegWrite), .Forward1(Forword1), .Forward2(Forword2),
    .ID_EX_Rs_en(id_ex_1_control_2_2[10]), .ID_EX_Rt_en(id_ex_1_control_2_2[11]));
  Multiplexer #(.width(16), .enable("false")) multiplexer_6 (
    .in0(dataredir_2_redirdata), .in1(Imm16), .out(multiplexer_6_out), .sel(id_ex_1_control_2[2]));
  ALU alu_1 (
    .dataA(dataredir_1_redirdata), .dataB(multiplexer_6_out), .Sel(id_ex_1_aluop_2), .ALUOut(alu_1_aluout),
    .equal(alu_1_equal), .gt(alu_1_gt));  // open: zero, carry, overflow
  EX_Mem ex_mem_1 (
    .clock(CLK), .equal(alu_1_equal), .gt(alu_1_gt), .BranchAddr(adder_2_out), .aluout(alu_1_aluout),
    .Control_2({ex_mem_1_control_2, PCSrc[1]}), .equal_2(ex_mem_1_equal_2), .gt_2(ex_mem_1_gt_2),
    .BranchAddr_2(BranchAddr), .aluout_2(ex_mem_1_aluout_2), .RegDst(multiplexer_5_out),
    .RegDst_2(Ex_Mem_Rd), .RD2(dataredir_2_redirdata), .RD2_2(ex_mem_1_rd2_2), .PC(PC3), .PC_2(PC4),
    .jAddr_2(JumpAddr), .jAddr(jumpaddr_1_jumpaddr_2), .Control(id_ex_1_control_2_2), .clear(Branch),
    .IR(EX_IR), .IR_2(MEM_IR));
  Branch branch_1 (
    .beq(ex_mem_1_control_2[1]), .ALU_beq(ex_mem_1_equal_2), .bnq(ex_mem_1_control_2[2]),
    .bgt(ex_mem_1_control_2[3]), .ALU_bgt(ex_mem_1_gt_2), .PCSrc(PCSrc[0]));
  assign controlled_buffer_1_out = ex_mem_1_control_2[4] ? ex_mem_1_rd2_2 : 16'bz;  // Controlled_Buffer controlled_buffer_1
  not not_4 (not_4_out, comparator_3_eq);
  Comparator #(.width(2)) comparator_3 (.a(PCSrc), .b(2'b00), .eq(comparator_3_eq));  // open: gt, lt
  Register #(.width(1), .trigger("falling")) register_3 (.D(not_4_out), .en(1'b1), .Q(Branch), .clk(CLK), .clr(clr));
  RAM #(.addrWidth(16), .dataWidth(16), .bus("separate")) ram_1 (
    .addr(ex_mem_1_aluout_2), .din(controlled_buffer_1_out), .data(RAMValue), .str(ex_mem_1_control_2[4]),
    .sel(1'b1), .clk(CLK), .ld(ex_mem_1_control_2[5]), .clr(clr));
  Mem_Wr mem_wr_1 (
    .Control(ex_mem_1_control_2[12:6]), .clock(CLK), .ALUOut(ex_mem_1_aluout_2), .MemOut(RAMValue),
    .RegDst(Ex_Mem_Rd),
    .Control_2({mem_wr_1_control_2[6:4], Halt, mem_wr_1_control_2[2], RegWrite, mem_wr_1_control_2[0]}),
    .clear(clr), .ALUOut_2(mem_wr_1_aluout_2), .MemOut_2(mem_wr_1_memout_2), .RegDst_2(mem_wr_1_regdst_2),
    .PC(PC4), .PC_2(PC5), .IR(MEM_IR), .IR_2(WR_IR));
  // Probe on multiplexer_7_out
  Multiplexer #(.width(16), .enable("false")) multiplexer_7 (
    .in0(mem_wr_1_aluout_2), .in1(mem_wr_1_memout_2), .out(multiplexer_7_out), .sel(mem_wr_1_control_2[0]));

  // Notes on the sheet:
  //   contents of rom_1 (hex, n*v repeats v):
  //   2000 3000 2100 350f 1000 1401 6200 6700 bb02 7300 7600 45ff a1f7 8010 0 0 4001 2100 350f a1f0 c000
  //   sign extend
  //   Mem2Reg
endmodule

module RF (
  input  [1:0] Read_register_1,
  input  [1:0] Read_register_2,
  input  [1:0] write_register,
  input  [15:0] write_data,
  input  RegWrite,
  input  clock,
  output [15:0] Reg_0_Value,
  output [15:0] Reg_1_Value,
  output [15:0] Reg_2_Value,
  output [15:0] Reg_3_Value,
  output [15:0] Read_Data_1,
  output [15:0] Read_Data_2
);

  wire [15:0] multiplexer_1_out, multiplexer_2_out, multiplexer_3_out, multiplexer_4_out;

  Multiplexer #(.select(3), .width(16), .enable("false")) multiplexer_1 (
    .in0(Reg_0_Value), .in1(Reg_0_Value), .in2(Reg_0_Value), .in3(Reg_0_Value), .in4(write_data),
    .in5(Reg_0_Value), .in6(Reg_0_Value), .in7(Reg_0_Value), .out(multiplexer_1_out),
    .sel({RegWrite, write_register}));
  Register #(.width(16), .trigger("falling")) register_1 (
    .D(multiplexer_1_out), .en(1'b1), .Q(Reg_0_Value), .clk(clock), .clr(1'b0));
  Register #(.width(16), .trigger("falling")) register_2 (
    .D(multiplexer_2_out), .en(1'b1), .Q(Reg_1_Value), .clk(clock), .clr(1'b0));
  Multiplexer #(.select(3), .width(16), .enable("false")) multiplexer_2 (
    .in0(Reg_1_Value), .in1(Reg_1_Value), .in2(Reg_1_Value), .in3(Reg_1_Value), .in4(Reg_1_Value),
    .in5(write_data), .in6(Reg_1_Value), .in7(Reg_1_Value), .out(multiplexer_2_out),
    .sel({RegWrite, write_register}));
  Register #(.width(16), .trigger("falling")) register_3 (
    .D(multiplexer_3_out), .en(1'b1), .Q(Reg_2_Value), .clk(clock), .clr(1'b0));
  Multiplexer #(.select(3), .width(16), .enable("false")) multiplexer_3 (
    .in0(Reg_2_Value), .in1(Reg_2_Value), .in2(Reg_2_Value), .in3(Reg_2_Value), .in4(Reg_2_Value),
    .in5(Reg_2_Value), .in6(write_data), .in7(Reg_2_Value), .out(multiplexer_3_out),
    .sel({RegWrite, write_register}));
  Multiplexer #(.select(3), .width(16), .enable("false")) multiplexer_4 (
    .in0(Reg_3_Value), .in1(Reg_3_Value), .in2(Reg_3_Value), .in3(Reg_3_Value), .in4(Reg_3_Value),
    .in5(Reg_3_Value), .in6(Reg_3_Value), .in7(write_data), .out(multiplexer_4_out),
    .sel({RegWrite, write_register}));
  Register #(.width(16), .trigger("falling")) register_4 (
    .D(multiplexer_4_out), .en(1'b1), .Q(Reg_3_Value), .clk(clock), .clr(1'b0));
  Multiplexer #(.select(2), .width(16), .enable("false")) multiplexer_5 (
    .in0(Reg_0_Value), .in1(Reg_1_Value), .in2(Reg_2_Value), .in3(Reg_3_Value), .out(Read_Data_1),
    .sel(Read_register_1));
  Multiplexer #(.select(2), .width(16), .enable("false")) multiplexer_6 (
    .in0(Reg_0_Value), .in1(Reg_1_Value), .in2(Reg_2_Value), .in3(Reg_3_Value), .out(Read_Data_2),
    .sel(Read_register_2));

  // Notes on the sheet:
  //   INPUTS
  //   These are INPUTS to the circuit
  //   OUTPUTS
endmodule

module IR (
  input  [15:0] Input,
  output [3:0] opcode,
  output [1:0] Rs,
  output [1:0] Rt,
  output [1:0] Rd,
  output [2:0] shamt,
  output [2:0] funct,
  output [11:0] jAddr,
  output [7:0] offset,
  output [7:0] imm
);


  assign funct = Input[2:0];
  assign imm = Input[7:0];
  assign jAddr = Input[11:0];
  assign offset = Input[7:0];
  assign opcode = Input[15:12];
  assign Rd = Input[7:6];
  assign Rs = Input[11:10];
  assign Rt = Input[9:8];
  assign shamt = Input[5:3];

  // Other names for the same wires on the sheet: op[3:0] = Input[15:12]

  // Notes on the sheet:
  //   From IM
  //   Outputs
endmodule

module ALU (
  input  [15:0] dataA,
  input  [15:0] dataB,
  input  [3:0] Sel,
  output carry,
  output overflow,
  output gt,
  output equal,
  output [15:0] ALUOut,
  output zero
);

  wire adder_1_cout, and_2_out, and_3_out, and_4_out, and_5_out, comparator_1_lt, not_1_out, not_2_out,
       not_3_out, not_4_out, or_2_out, or_3_out, subtractor_1_bout;
  wire [15:0] adder_1_out, and_out, bit_extender_1_out, OR_out, shifter_1_out, shifter_2_out, shifter_3_out,
       shifter_4_out, subtractor_1_out, XOR_out;

  Comparator #(.width(16)) comparator_1 (.a(dataA), .b(dataB), .gt(gt), .eq(equal), .lt(comparator_1_lt));
  Shifter #(.width(16)) shifter_1 (.in(dataB), .\dist (4'b1000), .out(shifter_1_out));
  Adder #(.width(16)) adder_1 (.a(dataA), .b(dataB), .out(adder_1_out), .cin(1'b0), .cout(adder_1_cout));
  Subtractor #(.width(16)) subtractor_1 (
    .a(dataA), .b(dataB), .out(subtractor_1_out), .bin(1'b0), .bout(subtractor_1_bout));
  assign and_out = dataA & dataB;  // AND_Gate and, 16 bits wide
  not not_1 (not_1_out, subtractor_1_out[15]);
  assign bit_extender_1_out = {{15{1'b0}}, comparator_1_lt};  // Bit_Extender bit_extender_1
  assign OR_out = dataA | dataB;  // OR_Gate OR, 16 bits wide
  assign XOR_out = dataA ^ dataB;  // XOR_Gate XOR, 16 bits wide
  Shifter #(.width(16)) shifter_2 (.in(dataA), .\dist (dataB[3:0]), .out(shifter_2_out));
  Shifter #(.width(16), .shift("lr")) shifter_3 (.in(dataA), .\dist (dataB[3:0]), .out(shifter_3_out));
  Shifter #(.width(16), .shift("ar")) shifter_4 (.in(dataA), .\dist (dataB[3:0]), .out(shifter_4_out));
  not not_2 (not_2_out, dataA[15]);
  and and_2 (and_2_out, dataA[15], dataB[15], not_1_out);
  not not_3 (not_3_out, dataB[15]);
  not not_4 (not_4_out, adder_1_out[15]);
  and and_3 (and_3_out, not_3_out, not_2_out, subtractor_1_out[15]);
  Multiplexer #(.select(4), .width(16)) multiplexer_1 (
    .in0(OR_out), .in1(and_out), .in2(adder_1_out), .in3(subtractor_1_out), .in4(shifter_2_out),
    .in5(shifter_3_out), .in6(shifter_4_out), .in7(bit_extender_1_out), .in8(shifter_1_out), .out(ALUOut),
    .sel(Sel), .en(1'b1));  // open: in9, in10, in11, in12, in13, in14, in15
  and and_4 (and_4_out, not_2_out, not_3_out, adder_1_out[15]);
  and and_5 (and_5_out, dataA[15], dataB[15], not_4_out);
  or or_2 (or_2_out, and_2_out, and_3_out);
  or or_3 (or_3_out, and_4_out, and_5_out);
  Multiplexer #(.select(2)) multiplexer_2 (
    .in0(adder_1_cout), .in1(subtractor_1_bout), .out(carry), .sel(Sel[1:0]), .en(1'b1));  // open: in2, in3
  nor nor_1 (zero, ALUOut[0], ALUOut[1], ALUOut[2], ALUOut[3], ALUOut[4], ALUOut[5], ALUOut[6], ALUOut[7], ALUOut[8], ALUOut[9], ALUOut[10], ALUOut[11], ALUOut[12], ALUOut[13], ALUOut[14], ALUOut[15]);
  Multiplexer #(.select(2)) multiplexer_3 (
    .in0(or_3_out), .in1(or_2_out), .out(overflow), .sel(Sel[1:0]), .en(1'b1));  // open: in2, in3

  // Notes on the sheet:
  //   Lui
endmodule

module Control (
  input  [15:0] IR,
  output [15:0] Control,
  output rsEnable_13,
  output rtEnable_14,
  output regWrite_10,
  output signExtend__0,
  output RegDst_1,
  output aluSource_2,
  output memToReg_9,
  output memWrite_7,
  output memRead_8,
  output display_11,
  output Jump_3,
  output beq_4,
  output bne_5,
  output bgt_6,
  output halt_12,
  output [3:0] aluFunc
);

  wire comparator_1_eq, multiplexer_3_out, not_1_out;
  wire [2:0] ir_1_funct;
  wire [3:0] bit_extender_1_out, ir_1_opcode;

  Comparator #(.width(16)) comparator_1 (.a({16{1'b0}}), .b(IR), .eq(comparator_1_eq));  // open: gt, lt
  IR ir_1 (.opcode(ir_1_opcode), .funct(ir_1_funct), .Input(IR));  // open: Rs, Rt, Rd, shamt, jAddr, offset, imm
  not not_1 (not_1_out, comparator_1_eq);
  Multiplexer #(.select(4), .enable("false")) multiplexer_1 (
    .in0(1'b1), .in1(1'b1), .in2(1'b0), .in3(1'b1), .in4(1'b1), .in5(1'b1), .in6(1'b1), .in7(1'b0),
    .in8(1'b0), .in9(1'b1), .in10(1'b1), .in11(1'b1), .in12(1'b0), .in13(1'b0), .in14(1'b0), .in15(1'b0),
    .out(Control[13]), .sel(ir_1_opcode));
  Multiplexer #(.select(4), .enable("false")) multiplexer_2 (
    .in0(1'b1), .in1(1'b0), .in2(1'b0), .in3(1'b0), .in4(1'b0), .in5(1'b0), .in6(1'b0), .in7(1'b1),
    .in8(1'b0), .in9(1'b1), .in10(1'b1), .in11(1'b1), .in12(1'b0), .in13(1'b0), .in14(1'b0), .in15(1'b0),
    .out(Control[14]), .sel(ir_1_opcode));
  Multiplexer #(.select(4), .enable("false")) multiplexer_3 (
    .in0(1'b1), .in1(1'b0), .in2(1'b1), .in3(1'b1), .in4(1'b1), .in5(1'b1), .in6(1'b1), .in7(1'b0),
    .in8(1'b0), .in9(1'b0), .in10(1'b0), .in11(1'b0), .in12(1'b0), .in13(1'b0), .in14(1'b0), .in15(1'b0),
    .out(multiplexer_3_out), .sel(ir_1_opcode));
  assign bit_extender_1_out = {{1{1'b0}}, ir_1_funct};  // Bit_Extender bit_extender_1
  Multiplexer #(.select(4), .enable("false")) multiplexer_4 (
    .in0(1'b0), .in1(1'b0), .in2(1'b0), .in3(1'b0), .in4(1'b1), .in5(1'b0), .in6(1'b1), .in7(1'b1),
    .in8(1'b0), .in9(1'b1), .in10(1'b1), .in11(1'b1), .in12(1'b0), .in13(1'b0), .in14(1'b0), .in15(1'b0),
    .out(Control[0]), .sel(ir_1_opcode));
  Multiplexer #(.select(4), .enable("false")) multiplexer_5 (
    .in0(1'b1), .in1(1'b0), .in2(1'b0), .in3(1'b0), .in4(1'b0), .in5(1'b0), .in6(1'b0), .in7(1'b0),
    .in8(1'b0), .in9(1'b0), .in10(1'b0), .in11(1'b0), .in12(1'b0), .in13(1'b0), .in14(1'b0), .in15(1'b0),
    .out(Control[1]), .sel(ir_1_opcode));
  Multiplexer #(.select(4), .width(4), .enable("false")) multiplexer_6 (
    .in0(bit_extender_1_out), .in2(4'b1000), .in3(4'b0000), .in4(4'b0010), .in5(4'b0001), .in6(4'b0010),
    .in7(4'b0010), .out(aluFunc), .sel(ir_1_opcode));  // open: in1, in8, in9, in10, in11, in12, in13, in14, in15
  Multiplexer #(.select(4), .enable("false")) multiplexer_7 (
    .in0(1'b0), .in1(1'b1), .in2(1'b1), .in3(1'b1), .in4(1'b1), .in5(1'b1), .in6(1'b1), .in7(1'b1),
    .in8(1'b0), .in9(1'b0), .in10(1'b0), .in11(1'b0), .in12(1'b1), .in13(1'b1), .in14(1'b1), .in15(1'b1),
    .out(aluSource_2), .sel(ir_1_opcode));
  and and_1 (Control[10], multiplexer_3_out, not_1_out);
  Multiplexer #(.select(4), .enable("false")) multiplexer_8 (
    .in0(1'b0), .in1(1'b0), .in2(1'b0), .in3(1'b0), .in4(1'b0), .in5(1'b0), .in6(1'b1), .in7(1'b0),
    .in8(1'b0), .in9(1'b0), .in10(1'b0), .in11(1'b0), .in12(1'b0), .in13(1'b0), .in14(1'b0), .in15(1'b0),
    .out(Control[9]), .sel(ir_1_opcode));
  Multiplexer #(.select(4), .enable("false")) multiplexer_9 (
    .in0(1'b0), .in1(1'b0), .in2(1'b0), .in3(1'b0), .in4(1'b0), .in5(1'b0), .in6(1'b0), .in7(1'b1),
    .in8(1'b0), .in9(1'b0), .in10(1'b0), .in11(1'b0), .in12(1'b0), .in13(1'b0), .in14(1'b0), .in15(1'b0),
    .out(Control[7]), .sel(ir_1_opcode));
  Multiplexer #(.select(4), .enable("false")) multiplexer_10 (
    .in0(1'b0), .in1(1'b0), .in2(1'b0), .in3(1'b0), .in4(1'b0), .in5(1'b0), .in6(1'b1), .in7(1'b0),
    .in8(1'b0), .in9(1'b0), .in10(1'b0), .in11(1'b0), .in12(1'b0), .in13(1'b0), .in14(1'b0), .in15(1'b0),
    .out(Control[8]), .sel(ir_1_opcode));
  Multiplexer #(.select(4), .enable("false")) multiplexer_11 (
    .in0(1'b0), .in1(1'b1), .in2(1'b0), .in3(1'b0), .in4(1'b0), .in5(1'b0), .in6(1'b0), .in7(1'b0),
    .in8(1'b0), .in9(1'b0), .in10(1'b0), .in11(1'b0), .in12(1'b0), .in13(1'b0), .in14(1'b0), .in15(1'b0),
    .out(Control[11]), .sel(ir_1_opcode));
  Comparator #(.width(4)) comparator_2 (.a(ir_1_opcode), .b(4'b1000), .eq(Control[3]));  // open: gt, lt
  Comparator #(.width(4)) comparator_3 (.a(ir_1_opcode), .b(4'b1001), .eq(beq_4));  // open: gt, lt
  Comparator #(.width(4)) comparator_4 (.a(ir_1_opcode), .b(4'b1010), .eq(bne_5));  // open: gt, lt
  Comparator #(.width(4)) comparator_5 (.a(ir_1_opcode), .b(4'b1011), .eq(bgt_6));  // open: gt, lt
  Comparator #(.width(4)) comparator_6 (.a(ir_1_opcode), .b(4'b1100), .eq(Control[12]));  // open: gt, lt

  assign {Control[15], Control[6:4], Control[2]} = {1'b0, bgt_6, bne_5, beq_4, aluSource_2};
  assign display_11 = Control[11];
  assign halt_12 = Control[12];
  assign Jump_3 = Control[3];
  assign memRead_8 = Control[8];
  assign memToReg_9 = Control[9];
  assign memWrite_7 = Control[7];
  assign RegDst_1 = Control[1];
  assign regWrite_10 = Control[10];
  assign rsEnable_13 = Control[13];
  assign rtEnable_14 = Control[14];
  assign signExtend__0 = Control[0];
endmodule

// SE
module SignExtend (
  input  [7:0] imm_offset,
  input  extendOp,
  output [15:0] extended_imm_offset
);

  wire [15:0] bit_extender_1_out, bit_extender_2_out;

  assign bit_extender_1_out = {{8{1'b0}}, imm_offset};  // Bit_Extender bit_extender_1
  assign bit_extender_2_out = {{8{imm_offset[7]}}, imm_offset};  // Bit_Extender bit_extender_2
  Multiplexer #(.width(16), .enable("false")) multiplexer_1 (
    .in0(bit_extender_1_out), .in1(bit_extender_2_out), .out(extended_imm_offset), .sel(extendOp));
endmodule

module Branch (
  input  beq,
  input  ALU_beq,
  input  bnq,
  input  bgt,
  input  ALU_bgt,
  output PCSrc
);

  wire and_1_out, and_2_out, and_3_out, not_1_out;

  not not_1 (not_1_out, ALU_beq);
  and and_1 (and_1_out, beq, ALU_beq);
  and and_2 (and_2_out, bnq, not_1_out);
  and and_3 (and_3_out, bgt, ALU_bgt);
  or or_1 (PCSrc, and_1_out, and_2_out, and_3_out);
endmodule

// JA
module JumpAddr (
  input  [15:0] PC,
  input  [11:0] JumpAddr,
  output [15:0] jumpAddr_2
);


  assign jumpAddr_2 = {PC[15:12], JumpAddr};
endmodule

// redir
module DataRedir (
  input  [1:0] Forward,
  input  [15:0] rawData,
  input  [15:0] memData,
  input  [15:0] wbData,
  output [15:0] redirData
);

  Multiplexer #(.select(2), .width(16), .enable("false")) multiplexer_1 (
    .in0(rawData), .in1(memData), .in2(wbData), .out(redirData), .sel(Forward));  // open: in3
endmodule

module IF_ID (
  input  enable,
  input  [15:0] PC_1,
  input  Clock,
  input  [15:0] Instruction,
  input  Clear,
  output [15:0] PC_1_2,
  output [15:0] Instruction_2
);

  wire register_3_q, reset;

  Register #(.width(16)) register_1 (.D(PC_1), .en(enable), .Q(PC_1_2), .clk(Clock), .clr(reset));
  Register #(.width(16)) register_2 (.D(Instruction), .en(enable), .Q(Instruction_2), .clk(Clock), .clr(reset));
  Register #(.width(1)) register_3 (.D(1'b1), .en(enable), .Q(register_3_q), .clk(Clock), .clr(reset));
  and and_1 (reset, Clear, register_3_q);

  // Other names for the same wires on the sheet: en = enable
endmodule

module ID_EX (
  input  clear,
  input  [15:0] Control,
  input  clock,
  input  [3:0] ALUOp,
  input  [15:0] RD1,
  input  [15:0] RD2,
  input  [1:0] Rt,
  input  [1:0] Rd,
  input  [15:0] pc_4,
  input  [7:0] imm_offset,
  input  [11:0] jAddr,
  input  [1:0] Rs,
  input  [15:0] IR,
  output [15:0] Control_2,
  output [3:0] ALUOp_2,
  output [15:0] RD1_2,
  output [15:0] RD2_2,
  output [1:0] Rt_2,
  output [1:0] Rd_2,
  output [15:0] Pc_4_2,
  output [7:0] imm_offset_2,
  output [11:0] jAddr_2,
  output [1:0] Rs_2,
  output [15:0] IR_2
);

  wire register_11_q, reset;
  wire [3:0] multiplexer_2_out;
  wire [15:0] multiplexer_1_out;

  Multiplexer #(.width(16), .enable("false")) multiplexer_1 (
    .in0(Control), .in1({16{1'b0}}), .out(multiplexer_1_out), .sel(1'b0));
  Multiplexer #(.width(4), .enable("false")) multiplexer_2 (
    .in0(ALUOp), .in1(4'b0000), .out(multiplexer_2_out), .sel(1'b0));
  Register #(.width(16)) register_1 (.D(multiplexer_1_out), .en(1'b1), .Q(Control_2), .clk(clock), .clr(reset));
  Register #(.width(4)) register_2 (.D(multiplexer_2_out), .en(1'b1), .Q(ALUOp_2), .clk(clock), .clr(reset));
  Register #(.width(16)) register_3 (.D(RD1), .en(1'b1), .Q(RD1_2), .clk(clock));  // open: clr
  Register #(.width(16)) register_4 (.D(RD2), .en(1'b1), .Q(RD2_2), .clk(clock));  // open: clr
  Register #(.width(2)) register_5 (.D(Rt), .en(1'b1), .Q(Rt_2), .clk(clock));  // open: clr
  Register #(.width(2)) register_6 (.D(Rd), .en(1'b1), .Q(Rd_2), .clk(clock));  // open: clr
  Register #(.width(16)) register_7 (.D(pc_4), .en(1'b1), .Q(Pc_4_2), .clk(clock));  // open: clr
  Register register_8 (.D(imm_offset), .en(1'b1), .Q(imm_offset_2), .clk(clock));  // open: clr
  Register #(.width(12)) register_9 (.D(jAddr), .en(1'b1), .Q(jAddr_2), .clk(clock));  // open: clr
  Register #(.width(2)) register_10 (.D(Rs), .en(1'b1), .Q(Rs_2), .clk(clock));  // open: clr
  Register #(.width(16)) u_IR (.D(IR), .en(1'b1), .Q(IR_2), .clk(clock));  // open: clr
  Register #(.width(1)) register_11 (.D(1'b1), .en(1'b1), .Q(register_11_q), .clk(clock), .clr(reset));
  and and_1 (reset, clear, register_11_q);
endmodule

module EX_Mem (
  input  clear,
  input  [12:0] Control,
  input  clock,
  input  equal,
  input  gt,
  input  [15:0] BranchAddr,
  input  [15:0] aluout,
  input  [1:0] RegDst,
  input  [15:0] RD2,
  input  [15:0] PC,
  input  [15:0] jAddr,
  input  [15:0] IR,
  output [12:0] Control_2,
  output equal_2,
  output gt_2,
  output [15:0] BranchAddr_2,
  output [15:0] aluout_2,
  output [1:0] RegDst_2,
  output [15:0] RD2_2,
  output [15:0] PC_2,
  output [15:0] jAddr_2,
  output [15:0] IR_2
);

  wire multiplexer_1_out, multiplexer_3_out, register_11_q, reset;
  wire [12:0] multiplexer_2_out;

  Multiplexer #(.enable("false")) multiplexer_1 (.in0(equal), .in1(1'b0), .out(multiplexer_1_out), .sel(1'b0));
  Multiplexer #(.width(13), .enable("false")) multiplexer_2 (
    .in0(Control), .in1({13{1'b0}}), .out(multiplexer_2_out), .sel(1'b0));
  Register #(.width(13)) register_1 (.D(multiplexer_2_out), .en(1'b1), .Q(Control_2), .clk(clock));  // open: clr
  Register #(.width(1)) register_2 (.D(multiplexer_1_out), .en(1'b1), .Q(equal_2), .clk(clock));  // open: clr
  Multiplexer #(.enable("false")) multiplexer_3 (.in0(gt), .in1(1'b0), .out(multiplexer_3_out), .sel(1'b0));
  Register #(.width(1)) register_3 (.D(multiplexer_3_out), .en(1'b1), .Q(gt_2), .clk(clock));  // open: clr
  Register #(.width(16)) register_4 (.D(BranchAddr), .en(1'b1), .Q(BranchAddr_2), .clk(clock), .clr(1'b0));
  Register #(.width(16)) register_5 (.D(aluout), .en(1'b1), .Q(aluout_2), .clk(clock), .clr(1'b0));
  Register #(.width(2)) register_6 (.D(RegDst), .en(1'b1), .Q(RegDst_2), .clk(clock), .clr(1'b0));
  Register #(.width(16)) register_7 (.D(RD2), .en(1'b1), .Q(RD2_2), .clk(clock), .clr(1'b0));
  Register #(.width(16)) register_8 (.D(PC), .en(1'b1), .Q(PC_2), .clk(clock), .clr(1'b0));
  Register #(.width(16)) register_9 (.D(jAddr), .en(1'b1), .Q(jAddr_2), .clk(clock), .clr(1'b0));
  Register #(.width(16)) register_10 (.D(IR), .en(1'b1), .Q(IR_2), .clk(clock), .clr(1'b0));
  Register #(.width(1)) register_11 (.D(1'b1), .en(1'b1), .Q(register_11_q), .clk(clock), .clr(reset));
  and and_1 (reset, clear, register_11_q);
endmodule

module Mem_Wr (
  input  [6:0] Control,
  input  clock,
  input  clear,
  input  [15:0] ALUOut,
  input  [15:0] MemOut,
  input  [1:0] RegDst,
  input  [15:0] PC,
  input  [15:0] IR,
  output [6:0] Control_2,
  output [15:0] ALUOut_2,
  output [15:0] MemOut_2,
  output [1:0] RegDst_2,
  output [15:0] PC_2,
  output [15:0] IR_2
);

  Register #(.width(7)) register_1 (.D(Control), .en(1'b1), .Q(Control_2), .clk(clock), .clr(clear));
  Register #(.width(16)) register_2 (.D(ALUOut), .en(1'b1), .Q(ALUOut_2), .clk(clock), .clr(clear));
  Register #(.width(16)) register_3 (.D(MemOut), .en(1'b1), .Q(MemOut_2), .clk(clock), .clr(clear));
  Register #(.width(2)) register_4 (.D(RegDst), .en(1'b1), .Q(RegDst_2), .clk(clock), .clr(clear));
  Register #(.width(16)) register_5 (.D(PC), .en(1'b1), .Q(PC_2), .clk(clock), .clr(clear));
  Register #(.width(16)) u_IR (.D(IR), .en(1'b1), .Q(IR_2), .clk(clock), .clr(clear));
endmodule

// DataHazards
module DataHazardsControl (
  input  ID_EX_Rs_en,
  input  EX_RegWrite,
  input  Mem_RegWrite,
  input  [1:0] EX_MEM_Rd,
  input  [1:0] MEM_WB_Rd,
  input  [1:0] ID_EX_Rs,
  input  [1:0] ID_EX_Rt,
  input  ID_EX_Rt_en,
  output [1:0] Forward1,
  output [1:0] Forward2
);

  wire comparator_1_eq, comparator_2_eq, comparator_3_eq, comparator_4_eq;
  wire [1:0] and_3_out, and_4_out, multiplexer_1_out, multiplexer_2_out, multiplexer_3_out,
       multiplexer_4_out, multiplexer_5_out, multiplexer_6_out, multiplexer_7_out, multiplexer_8_out;

  Comparator #(.width(2)) comparator_1 (.a(EX_MEM_Rd), .b(ID_EX_Rs), .eq(comparator_1_eq));  // open: gt, lt
  Comparator #(.width(2)) comparator_2 (.a(EX_MEM_Rd), .b(ID_EX_Rt), .eq(comparator_2_eq));  // open: gt, lt
  Comparator #(.width(2)) comparator_3 (.a(MEM_WB_Rd), .b(ID_EX_Rs), .eq(comparator_3_eq));  // open: gt, lt
  Comparator #(.width(2)) comparator_4 (.a(MEM_WB_Rd), .b(ID_EX_Rt), .eq(comparator_4_eq));  // open: gt, lt
  and and_1 (and_3_out[1], EX_RegWrite, comparator_1_eq);
  and and_2 (and_4_out[1], EX_RegWrite, comparator_2_eq);
  and and_3 (and_3_out[0], Mem_RegWrite, comparator_3_eq);
  and and_4 (and_4_out[0], Mem_RegWrite, comparator_4_eq);
  Multiplexer #(.width(2), .enable("false")) multiplexer_1 (
    .in0(2'b00), .in1(2'b10), .out(multiplexer_1_out), .sel(and_3_out[1]));
  Multiplexer #(.width(2), .enable("false")) multiplexer_2 (
    .in0(2'b00), .in1(2'b01), .out(multiplexer_2_out), .sel(and_3_out[0]));
  Multiplexer #(.width(2), .enable("false")) multiplexer_3 (
    .in0(2'b00), .in1(2'b10), .out(multiplexer_3_out), .sel(and_4_out[1]));
  Multiplexer #(.width(2), .enable("false")) multiplexer_4 (
    .in0(2'b00), .in1(2'b01), .out(multiplexer_4_out), .sel(and_4_out[0]));
  Multiplexer #(.select(2), .width(2), .enable("false")) multiplexer_5 (
    .in0(2'b00), .in1(2'b01), .in2(2'b10), .in3(2'b10), .out(multiplexer_5_out), .sel(and_3_out));
  Multiplexer #(.select(2), .width(2), .enable("false")) multiplexer_6 (
    .in0(2'b00), .in1(2'b01), .in2(2'b10), .in3(2'b10), .out(multiplexer_6_out), .sel(and_4_out));
  Multiplexer #(.select(2), .width(2), .enable("false")) multiplexer_7 (
    .in0(2'b00), .in1(multiplexer_2_out), .in2(multiplexer_1_out), .in3(multiplexer_5_out),
    .out(multiplexer_7_out), .sel({EX_RegWrite, Mem_RegWrite}));
  Multiplexer #(.select(2), .width(2), .enable("false")) multiplexer_8 (
    .in0(2'b00), .in1(multiplexer_4_out), .in2(multiplexer_3_out), .in3(multiplexer_6_out),
    .out(multiplexer_8_out), .sel({EX_RegWrite, Mem_RegWrite}));
  Multiplexer #(.width(2), .enable("false")) multiplexer_9 (
    .in0(2'b00), .in1(multiplexer_7_out), .out(Forward1), .sel(ID_EX_Rs_en));
  Multiplexer #(.width(2), .enable("false")) multiplexer_10 (
    .in0(2'b00), .in1(multiplexer_8_out), .out(Forward2), .sel(ID_EX_Rt_en));

  // Notes on the sheet:
  //   high
endmodule

module Load_useControl (
  input  [15:0] IR,
  input  ID_EX_MemRead,
  input  [1:0] ID_EX_Rt,
  input  ID_EX_Rs_en,
  input  [1:0] IF_ID_Rs,
  input  ID_EX_Rt_en,
  input  [1:0] IF_ID_Rt,
  output load_use
);

  wire and_1_out, and_2_out, and_3_out, comparator_1_eq, comparator_2_eq, comparator_3_eq, or_1_out;
  wire [3:0] ir_1_opcode;

  IR ir_1 (.opcode(ir_1_opcode), .Input(IR));  // open: Rs, Rt, Rd, shamt, funct, jAddr, offset, imm
  Comparator #(.width(4)) comparator_1 (.a(4'b0110), .b(ir_1_opcode), .eq(comparator_1_eq));  // open: gt, lt
  Comparator #(.width(2)) comparator_2 (.a(ID_EX_Rt), .b(IF_ID_Rs), .eq(comparator_2_eq));  // open: gt, lt
  Comparator #(.width(2)) comparator_3 (.a(ID_EX_Rt), .b(IF_ID_Rt), .eq(comparator_3_eq));  // open: gt, lt
  and and_1 (and_1_out, ID_EX_Rs_en, comparator_2_eq);
  and and_2 (and_2_out, ID_EX_Rt_en, comparator_3_eq);
  or or_1 (or_1_out, and_1_out, and_2_out);
  and and_3 (and_3_out, ID_EX_MemRead, or_1_out);
  Multiplexer #(.enable("false")) multiplexer_1 (.in0(1'b0), .in1(and_3_out), .out(load_use), .sel(comparator_1_eq));
endmodule
