// Logisim project CPU-singleClock.circ as structural Verilog: 5 circuits, main circuit main
module main (
  input  clr
);

  wire alu_1_equal, alu_1_great, ALUSrc, and_2_out, and_3_out, and_4_out, beq, bne, bqt, CLK, clock_1_out,
       comparator_1_eq, comparator_2_eq, display, Halt, jump, memRead, memToReg, memWrite, multiplexer_6_out,
       multiplexer_7_out, not_1_out, not_2_out, not_3_out, PCSrc, RegDst, RegWrite, signExtend;
  wire [1:0] multiplexer_4_out;
  wire [2:0] funct;
  wire [3:0] aluFunc, op;
  wire [7:3] imm;
  wire [11:0] PC;
  wire [15:0] adder_2_out, alu_1_out_8, bit_extender_1_out, bit_extender_2_out, CLKCounter,
       controlled_buffer_1_out, controlled_buffer_2_out, d0, d1, extendedImm, multiplexer_1_out,
       multiplexer_5_out, multiplexer_8_out, nextPc, pcPlus1, R_rs, R_rt, RAMValue, rf_1_reg_0_value,
       rf_1_reg_1_value, rf_1_reg_2_value, rf_1_reg_3_value;
  wire [15:8] jAddr;

  Clock clock_1 (.out(clock_1_out));
  // Probe on R_rs
  // Probe on R_rt
  // Probe on RAMValue
  // Probe on CLKCounter
  and and_1 (CLK, clock_1_out, not_1_out);
  not not_1 (not_1_out, Halt);
  // Probe on {jAddr[15:12], PC}
  Register #(.width(16)) register_1 (.D(nextPc), .en(1'b1), .Q({jAddr[15:12], PC}), .clk(CLK), .clr(clr));
  // Probe on {op, jAddr[11:8], imm, funct}
  Adder #(.width(16)) adder_1 (.a({jAddr[15:12], PC}), .b(16'h1), .out(pcPlus1));  // open: cin, cout
  Adder #(.width(16)) adder_2 (.a(pcPlus1), .b(extendedImm), .out(adder_2_out));  // open: cin, cout
  Counter #(.width(16), .max('hffff), .ongoal("continue")) counter_1 (
    .count(1'b1), .Q(CLKCounter), .clk(CLK));  // open: load, D, carry, clr
  Multiplexer #(.width(16), .enable("false")) multiplexer_1 (
    .in0(pcPlus1), .in1(adder_2_out), .out(multiplexer_1_out), .sel(PCSrc));
  // Probe on nextPc
  Multiplexer #(.width(16), .enable("false")) multiplexer_2 (
    .in0(multiplexer_1_out), .in1({jAddr, imm, funct}), .out(nextPc), .sel(jump));
  Control control_1 (
    .op(op), .func(funct), .beq(beq), .aluSource(ALUSrc), .memToReg(memToReg), .bne(bne),
    .memWrite(memWrite), .memRead(memRead), .bgt(bqt), .display(display), .Jump(jump), .regWrite(RegWrite),
    .signExtend(signExtend), .RegDst(RegDst), .aluFunc(aluFunc), .halt(Halt));
  ROM #(.addrWidth(16), .dataWidth(16)) rom_1 (
    .addr({jAddr[15:12], PC}), .data({op, jAddr[11:8], imm, funct}), .sel(1'b1));
  // Probe on multiplexer_8_out
  // Probe on {imm, funct}
  assign bit_extender_1_out = {{8{1'b0}}, {imm, funct}};  // Bit_Extender bit_extender_1
  assign bit_extender_2_out = {{8{imm[7]}}, {imm, funct}};  // Bit_Extender bit_extender_2
  // Probe on rf_1_reg_0_value
  // Probe on jAddr[11:10]
  // Probe on jAddr[9:8]
  assign controlled_buffer_1_out = not_2_out ? multiplexer_8_out : 16'bz;  // Controlled_Buffer controlled_buffer_1
  not not_2 (not_2_out, CLK);
  // Probe on extendedImm
  Multiplexer #(.width(16), .enable("false")) multiplexer_3 (
    .in0(bit_extender_1_out), .in1(bit_extender_2_out), .out(extendedImm), .sel(signExtend));
  // Probe on rf_1_reg_1_value
  // Probe on rf_1_reg_2_value
  // Probe on R_rt
  RF rf_1 (
    .Read_register_1(jAddr[11:10]), .Read_register_2(jAddr[9:8]), .write_register(multiplexer_4_out),
    .write_data(controlled_buffer_1_out), .Read_Data_1(R_rs), .Read_Data_2(R_rt),
    .Reg_0_Value(rf_1_reg_0_value), .Reg_1_Value(rf_1_reg_1_value), .Reg_2_Value(rf_1_reg_2_value),
    .Reg_3_Value(rf_1_reg_3_value), .RegWrite(RegWrite), .clock(CLK));
  Multiplexer #(.width(2), .enable("false")) multiplexer_4 (
    .in0(jAddr[9:8]), .in1(imm[7:6]), .out(multiplexer_4_out), .sel(RegDst));
  // Probe on imm[7:6]
  // Probe on rf_1_reg_3_value
  // Probe on multiplexer_5_out
  Multiplexer #(.width(16), .enable("false")) multiplexer_5 (
    .in0(R_rt), .in1(extendedImm), .out(multiplexer_5_out), .sel(ALUSrc));
  // Probe on aluFunc
  Comparator comparator_1 (.a(8'h1), .b({imm, funct}), .eq(comparator_1_eq));  // open: gt, lt
  not not_3 (not_3_out, alu_1_equal);
  // Probe on alu_1_out_8
  ALU alu_1 (
    .in_1(R_rs), .in_2(multiplexer_5_out), .in_3(aluFunc), .out_8(alu_1_out_8), .equal(alu_1_equal),
    .great(alu_1_great));  // open: zero, carry, Overflow
  Register #(.width(16)) register_2 (.D(R_rs), .en(multiplexer_6_out), .Q(d0), .clk(CLK), .clr(1'b0));
  Multiplexer #(.enable("false")) multiplexer_6 (
    .in0(display), .in1(1'b0), .out(multiplexer_6_out), .sel(comparator_1_eq));
  Multiplexer #(.enable("false")) multiplexer_7 (
    .in0(display), .in1(1'b0), .out(multiplexer_7_out), .sel(comparator_2_eq));
  Comparator comparator_2 (.a({8{1'b0}}), .b({imm, funct}), .eq(comparator_2_eq));  // open: gt, lt
  and and_2 (and_2_out, beq, alu_1_equal);
  and and_3 (and_3_out, bne, not_3_out);
  and and_4 (and_4_out, bqt, alu_1_great);
  assign controlled_buffer_2_out = memWrite ? R_rt : 16'bz;  // Controlled_Buffer controlled_buffer_2
  Hex_Digit_Display hex_digit_display_1 (.value(d0[15:12]));  // open: dp
  Register #(.width(16)) register_3 (.D(R_rs), .en(multiplexer_7_out), .Q(d1), .clk(CLK), .clr(1'b0));
  Hex_Digit_Display hex_digit_display_2 (.value(d1[15:12]));  // open: dp
  or or_1 (PCSrc, and_2_out, and_3_out, and_4_out);
  Hex_Digit_Display hex_digit_display_3 (.value(d0[11:8]));  // open: dp
  Hex_Digit_Display hex_digit_display_4 (.value(d0[7:4]));  // open: dp
  Hex_Digit_Display hex_digit_display_5 (.value(d1[11:8]));  // open: dp
  Hex_Digit_Display hex_digit_display_6 (.value(d1[7:4]));  // open: dp
  RAM #(.addrWidth(16), .dataWidth(16), .bus("separate")) ram_1 (
    .addr(alu_1_out_8), .din(controlled_buffer_2_out), .data(RAMValue), .str(memWrite), .sel(1'b1),
    .clk(CLK), .ld(memRead), .clr(clr));
  Hex_Digit_Display hex_digit_display_7 (.value(d0[3:0]));  // open: dp
  Hex_Digit_Display hex_digit_display_8 (.value(d1[3:0]));  // open: dp
  Multiplexer #(.width(16), .enable("false")) multiplexer_8 (
    .in0(alu_1_out_8), .in1(RAMValue), .out(multiplexer_8_out), .sel(memToReg));

  // Other names for the same wires on the sheet: imm[2:0] = funct; jAddr[7:0] = {imm, funct};
  //   offset[7:0] = {imm, funct}; shamt[2:0] = imm[5:3]; rd[1:0] = imm[7:6]; rt[1:0] = jAddr[9:8];
  //   rs[1:0] = jAddr[11:10]; PC[15:12] = jAddr[15:12]

  // Notes on the sheet:
  //   From IM
  //   just track
  //   PC
  //   IM
  //   contents of rom_1 (hex, n*v repeats v):
  //   2000 3000 2100 350f 1000 1401 6200 6700 bb02 7600 7300 45ff a1f7 8010 0 0 4001 2100 350f a1f0 c000
endmodule

module RF (
  input  [1:0] Read_register_1,
  input  [1:0] Read_register_2,
  input  [1:0] write_register,
  input  [15:0] write_data,
  input  RegWrite,
  input  clock,
  output [15:0] Reg_0_Value,
  output [15:0] Reg_1_Value,
  output [15:0] Reg_2_Value,
  output [15:0] Reg_3_Value,
  output [15:0] Read_Data_1,
  output [15:0] Read_Data_2
);

  wire [15:0] multiplexer_1_out, multiplexer_2_out, multiplexer_3_out, multiplexer_4_out;

  Multiplexer #(.select(3), .width(16), .enable("false")) multiplexer_1 (
    .in0(Reg_0_Value), .in1(Reg_0_Value), .in2(Reg_0_Value), .in3(Reg_0_Value), .in4(write_data),
    .in5(Reg_0_Value), .in6(Reg_0_Value), .in7(Reg_0_Value), .out(multiplexer_1_out),
    .sel({RegWrite, write_register}));
  Register #(.width(16)) register_1 (.D(multiplexer_1_out), .en(1'b1), .Q(Reg_0_Value), .clk(clock), .clr(1'b0));
  Register #(.width(16)) register_2 (.D(multiplexer_2_out), .en(1'b1), .Q(Reg_1_Value), .clk(clock), .clr(1'b0));
  Multiplexer #(.select(3), .width(16), .enable("false")) multiplexer_2 (
    .in0(Reg_1_Value), .in1(Reg_1_Value), .in2(Reg_1_Value), .in3(Reg_1_Value), .in4(Reg_1_Value),
    .in5(write_data), .in6(Reg_1_Value), .in7(Reg_1_Value), .out(multiplexer_2_out),
    .sel({RegWrite, write_register}));
  Register #(.width(16)) register_3 (.D(multiplexer_3_out), .en(1'b1), .Q(Reg_2_Value), .clk(clock), .clr(1'b0));
  Multiplexer #(.select(3), .width(16), .enable("false")) multiplexer_3 (
    .in0(Reg_2_Value), .in1(Reg_2_Value), .in2(Reg_2_Value), .in3(Reg_2_Value), .in4(Reg_2_Value),
    .in5(Reg_2_Value), .in6(write_data), .in7(Reg_2_Value), .out(multiplexer_3_out),
    .sel({RegWrite, write_register}));
  Multiplexer #(.select(3), .width(16), .enable("false")) multiplexer_4 (
    .in0(Reg_3_Value), .in1(Reg_3_Value), .in2(Reg_3_Value), .in3(Reg_3_Value), .in4(Reg_3_Value),
    .in5(Reg_3_Value), .in6(Reg_3_Value), .in7(write_data), .out(multiplexer_4_out),
    .sel({RegWrite, write_register}));
  Register #(.width(16)) register_4 (.D(multiplexer_4_out), .en(1'b1), .Q(Reg_3_Value), .clk(clock), .clr(1'b0));
  Multiplexer #(.select(2), .width(16), .enable("false")) multiplexer_5 (
    .in0(Reg_0_Value), .in1(Reg_1_Value), .in2(Reg_2_Value), .in3(Reg_3_Value), .out(Read_Data_1),
    .sel(Read_register_1));
  Multiplexer #(.select(2), .width(16), .enable("false")) multiplexer_6 (
    .in0(Reg_0_Value), .in1(Reg_1_Value), .in2(Reg_2_Value), .in3(Reg_3_Value), .out(Read_Data_2),
    .sel(Read_register_2));

  // Notes on the sheet:
  //   INPUTS
  //   These are INPUTS to the circuit
  //   OUTPUTS
endmodule

module IR (
  input  [15:0] Input,
  output [3:0] Outputs,
  output [1:0] out_3,
  output [1:0] out_4,
  output [1:0] out_5,
  output [2:0] out_6,
  output [2:0] out_7,
  output [7:0] out_8,
  output [15:0] out_9
);

  wire signExtend;
  wire [15:0] bit_extender_1_out, bit_extender_2_out, extendedImm;

  assign bit_extender_1_out = {{8{1'b0}}, Input[7:0]};  // Bit_Extender bit_extender_1
  assign bit_extender_2_out = {{8{Input[7]}}, Input[7:0]};  // Bit_Extender bit_extender_2
  Multiplexer #(.width(16), .enable("false")) multiplexer_1 (
    .in0(bit_extender_1_out), .in1(bit_extender_2_out), .out(extendedImm), .sel(signExtend));

  assign out_3 = Input[11:10];
  assign out_4 = Input[9:8];
  assign out_5 = Input[7:6];
  assign out_6 = Input[5:3];
  assign out_7 = Input[2:0];
  assign out_8 = Input[7:0];
  assign out_9[11:0] = Input[11:0];
  assign Outputs = Input[15:12];

  // Other names for the same wires on the sheet: op[3:0] = Input[15:12]; funct[2:0] = Input[2:0];
  //   imm[7:0] = Input[7:0]; jAddr[15:0] = {out_9[15:12], Input[11:0]}; offset[7:0] = Input[7:0];
  //   shamt[2:0] = Input[5:3]; rd[1:0] = Input[7:6]; rt[1:0] = Input[9:8]; rs[1:0] = Input[11:10];
  //   PC[15:12] = out_9[15:12]

  // Notes on the sheet:
  //   From IM
endmodule

module ALU (
  input  [15:0] in_1,
  input  [15:0] in_2,
  input  [3:0] in_3,
  output carry,
  output Overflow,
  output great,
  output equal,
  output [15:0] out_8,
  output zero
);

  wire adder_1_cout, and_2_out, and_3_out, and_4_out, and_5_out, comparator_1_lt, not_1_out, not_2_out,
       not_3_out, not_4_out, or_2_out, or_3_out, subtractor_1_bout;
  wire [15:0] adder_1_out, and_out, bit_extender_1_out, OR_out, shifter_1_out, shifter_2_out, shifter_3_out,
       shifter_4_out, subtractor_1_out, XOR_out;

  Comparator #(.width(16)) comparator_1 (.a(in_1), .b(in_2), .gt(great), .eq(equal), .lt(comparator_1_lt));
  Shifter #(.width(16)) shifter_1 (.in(in_2), .\dist (4'b1000), .out(shifter_1_out));
  Adder #(.width(16)) adder_1 (.a(in_1), .b(in_2), .out(adder_1_out), .cin(1'b0), .cout(adder_1_cout));
  Subtractor #(.width(16)) subtractor_1 (
    .a(in_1), .b(in_2), .out(subtractor_1_out), .bin(1'b0), .bout(subtractor_1_bout));
  assign and_out = in_1 & in_2;  // AND_Gate and, 16 bits wide
  not not_1 (not_1_out, subtractor_1_out[15]);
  assign bit_extender_1_out = {{15{1'b0}}, comparator_1_lt};  // Bit_Extender bit_extender_1
  assign OR_out = in_1 | in_2;  // OR_Gate OR, 16 bits wide
  assign XOR_out = in_1 ^ in_2;  // XOR_Gate XOR, 16 bits wide
  Shifter #(.width(16)) shifter_2 (.in(in_1), .\dist (in_2[3:0]), .out(shifter_2_out));
  Shifter #(.width(16), .shift("lr")) shifter_3 (.in(in_1), .\dist (in_2[3:0]), .out(shifter_3_out));
  Shifter #(.width(16), .shift("ar")) shifter_4 (.in(in_1), .\dist (in_2[3:0]), .out(shifter_4_out));
  not not_2 (not_2_out, in_1[15]);
  and and_2 (and_2_out, in_1[15], in_2[15], not_1_out);
  not not_3 (not_3_out, in_2[15]);
  not not_4 (not_4_out, adder_1_out[15]);
  and and_3 (and_3_out, not_3_out, not_2_out, subtractor_1_out[15]);
  Multiplexer #(.select(4), .width(16)) multiplexer_1 (
    .in0(OR_out), .in1(and_out), .in2(adder_1_out), .in3(subtractor_1_out), .in4(shifter_2_out),
    .in5(shifter_3_out), .in6(shifter_4_out), .in7(bit_extender_1_out), .in8(shifter_1_out), .out(out_8),
    .sel(in_3), .en(1'b1));  // open: in9, in10, in11, in12, in13, in14, in15
  and and_4 (and_4_out, not_2_out, not_3_out, adder_1_out[15]);
  and and_5 (and_5_out, in_1[15], in_2[15], not_4_out);
  or or_2 (or_2_out, and_2_out, and_3_out);
  or or_3 (or_3_out, and_4_out, and_5_out);
  Multiplexer #(.select(2)) multiplexer_2 (
    .in0(adder_1_cout), .in1(subtractor_1_bout), .out(carry), .sel(in_3[1:0]), .en(1'b1));  // open: in2, in3
  nor nor_1 (zero, out_8[0], out_8[1], out_8[2], out_8[3], out_8[4], out_8[5], out_8[6], out_8[7], out_8[8], out_8[9], out_8[10], out_8[11], out_8[12], out_8[13], out_8[14], out_8[15]);
  Multiplexer #(.select(2)) multiplexer_3 (
    .in0(or_3_out), .in1(or_2_out), .out(Overflow), .sel(in_3[1:0]), .en(1'b1));  // open: in2, in3

  // Notes on the sheet:
  //   A
  //   B
  //   Lui
  //   selector
endmodule

module Control (
  input  [3:0] op,
  input  [2:0] func,
  output beq,
  output regWrite,
  output signExtend,
  output RegDst,
  output bne,
  output aluSource,
  output memToReg,
  output bgt,
  output memWrite,
  output memRead,
  output halt,
  output display,
  output Jump,
  output [3:0] aluFunc
);

  wire [3:0] bit_extender_1_out;

  Comparator #(.width(4)) comparator_1 (.a(op), .b(4'b1001), .eq(beq));  // open: gt, lt
  Comparator #(.width(4)) comparator_2 (.a(op), .b(4'b1010), .eq(bne));  // open: gt, lt
  Comparator #(.width(4)) comparator_3 (.a(op), .b(4'b1011), .eq(bgt));  // open: gt, lt
  Comparator #(.width(4)) comparator_4 (.a(op), .b(4'b1100), .eq(halt));  // open: gt, lt
  Multiplexer #(.select(4), .enable("false")) multiplexer_1 (
    .in0(1'b1), .in2(1'b1), .in3(1'b1), .in4(1'b1), .in5(1'b1), .in6(1'b1), .out(regWrite), .sel(op));  // open: in1, in7, in8, in9, in10, in11, in12, in13, in14, in15
  assign bit_extender_1_out = {{1{1'b0}}, func};  // Bit_Extender bit_extender_1
  Multiplexer #(.select(4), .enable("false")) multiplexer_2 (
    .in0(1'b0), .in1(1'b0), .in2(1'b0), .in3(1'b0), .in4(1'b1), .in5(1'b0), .in6(1'b1), .in7(1'b1),
    .in8(1'b0), .in9(1'b1), .in10(1'b1), .in11(1'b1), .in12(1'b0), .in13(1'b0), .in14(1'b0), .in15(1'b0),
    .out(signExtend), .sel(op));
  Multiplexer #(.select(4), .enable("false")) multiplexer_3 (
    .in0(1'b1), .in2(1'b0), .in3(1'b0), .in4(1'b0), .in5(1'b0), .in6(1'b0), .out(RegDst), .sel(op));  // open: in1, in7, in8, in9, in10, in11, in12, in13, in14, in15
  Multiplexer #(.select(4), .width(4), .enable("false")) multiplexer_4 (
    .in0(bit_extender_1_out), .in2(4'b1000), .in3(4'b0000), .in4(4'b0010), .in5(4'b0001), .in6(4'b0010),
    .in7(4'b0010), .out(aluFunc), .sel(op));  // open: in1, in8, in9, in10, in11, in12, in13, in14, in15
  Multiplexer #(.select(4), .enable("false")) multiplexer_5 (
    .in0(1'b0), .in1(1'b1), .in2(1'b1), .in3(1'b1), .in4(1'b1), .in5(1'b1), .in6(1'b1), .in7(1'b1),
    .in9(1'b0), .in10(1'b0), .in11(1'b0), .in12(1'b1), .in13(1'b1), .in14(1'b1), .in15(1'b1),
    .out(aluSource), .sel(op));  // open: in8
  Multiplexer #(.select(4), .enable("false")) multiplexer_6 (
    .in0(1'b0), .in2(1'b0), .in3(1'b0), .in4(1'b0), .in5(1'b0), .in6(1'b1), .in7(1'b0), .out(memToReg),
    .sel(op));  // open: in1, in8, in9, in10, in11, in12, in13, in14, in15
  Multiplexer #(.select(4), .enable("false")) multiplexer_7 (
    .in0(1'b0), .in1(1'b0), .in2(1'b0), .in3(1'b0), .in4(1'b0), .in5(1'b0), .in6(1'b0), .in7(1'b1),
    .in8(1'b0), .in9(1'b0), .in10(1'b0), .in11(1'b0), .in12(1'b0), .in13(1'b0), .in14(1'b0), .in15(1'b0),
    .out(memWrite), .sel(op));
  Multiplexer #(.select(4), .enable("false")) multiplexer_8 (
    .in0(1'b0), .in1(1'b0), .in2(1'b0), .in3(1'b0), .in4(1'b0), .in5(1'b0), .in6(1'b1), .in7(1'b0),
    .in8(1'b0), .in9(1'b0), .in10(1'b0), .in11(1'b0), .in12(1'b0), .in13(1'b0), .in14(1'b0), .in15(1'b0),
    .out(memRead), .sel(op));
  Multiplexer #(.select(4), .enable("false")) multiplexer_9 (
    .in0(1'b0), .in1(1'b1), .in2(1'b0), .in3(1'b0), .in4(1'b0), .in5(1'b0), .in6(1'b0), .in7(1'b0),
    .in8(1'b0), .in9(1'b0), .in10(1'b0), .in11(1'b0), .in12(1'b0), .in13(1'b0), .in14(1'b0), .in15(1'b0),
    .out(display), .sel(op));
  Comparator #(.width(4)) comparator_5 (.a(op), .b(4'b1000), .eq(Jump));  // open: gt, lt
endmodule
